# Fritzing sketch CL_UVScanner (saved by Fritzing 0.9.3b)
breadboards: 2

parts:
  Part1 = Arduino Nano (Rev3.0)
  R3 = Resistor [tolerance=±5% resistance=10k package="2512 [SMD]"]
  R4 = Resistor [tolerance=±5% resistance=10k package="2512 [SMD]"]
  ROTARY_ENCODER1 = ENCODER-QUADRATURE [package=encoder-16mm-quad]
  ENCODER_SW1 = Pushbutton [package=THT]
  4_Digit_Display1 = Grove 4 Digit Display
  Q1 = MOSFET-NCHANNEL [part_number=FS10KM package=to220v]
  R3_2 = Resistor [tolerance=±1% resistance=120 package="2512 [SMD]"]
  J1 = Piezo Speaker
  DC_12V = Power plug
  +_LED_STRIP_- = male pin header, 2 pins [form="♂ (male)"]
  R5 = Resistor [tolerance=±1% resistance=120 package="2512 [SMD]"]
  Start = SWITCH-MOMENTARY-2 [package=tactile-pth-12mm]
  Stop = SWITCH-MOMENTARY-2 [package=tactile-pth-12mm]

nets:
  GND: Part1.GND, ROTARY_ENCODER1.B, ENCODER_SW1.leg0, 4_Digit_Display1.GND, Q1.S, DC_12V.GND, Start.2, Stop.2
  N1: Part1.D2, R3.Pin_0, ROTARY_ENCODER1.A
  N2: Part1.D3, R4.Pin_0, ROTARY_ENCODER1.C
  N3: Part1.D4, ENCODER_SW1.leg1
  N4: Part1.D6, Start.1
  N5: Part1.D7, Stop.1
  N6: Part1.D8, R5.Pin_1
  N7: Part1.D9, R3_2.Pin_0
  N8: Part1.D10, J1.pin1
  N9: Part1.D11/MOSI, 4_Digit_Display1.DIO
  N10: Part1.D12/MISO, 4_Digit_Display1.CLK
  VIN: Part1.VIN, DC_12V.VCC, +_LED_STRIP_-.pin1
  5V: Part1.5V, R3.Pin_1, R4.Pin_1, 4_Digit_Display1.VCC
  N11: Q1.G, R5.Pin_0
  N12: Q1.D, +_LED_STRIP_-.pin2
  N13: R3_2.Pin_1, J1.pin2

notes:
  ROT ENCODER SW
